# Fritzing sketch Шаблон электросхемы проекта-рома (saved by Fritzing 0.9.3b)
breadboards: 1

parts:
  Часть1 = Arduino Uno (Rev3)
  VCC1 = Battery
  S1 = Toggle Switch [package=THT]
  Часть2 = LED Matrix - Serial Interface - Red/Green/Blue
  SP1 = SPEAKER [package=pcb_mount_speaker]
  S2 = Pushbutton [package="[THT]"]
  S3 = Pushbutton [package="[THT]"]
  S4 = Pushbutton [package="[THT]"]
  S5 = Pushbutton [package="[THT]"]
  Q1 = NPN-Transistor [package="TO92 [THT]"]

nets:
  N1: Часть1.D2, SP1.-, Q1.E
  N2: Часть1.D3_PWM, Часть2.MOSI
  N3: Часть1.D4, S2.Pin_3, S2.Pin_4
  N4: Часть1.D5_PWM, S5.Pin_3, S5.Pin_4
  N5: Часть1.D6_PWM, S3.Pin_3, S3.Pin_4
  N6: Часть1.D7, S4.Pin_3, S4.Pin_4
  N7: Часть1.GND, S1.L2, Часть2.SCK, SP1.+, S2.Pin_1, S2.Pin_2, S3.Pin_1, S3.Pin_2, S4.Pin_1, S4.Pin_2, S5.Pin_1, S5.Pin_2
  VIN: Часть1.VIN, VCC1.+, Часть2.VCC, Q1.C
  N8: VCC1.-, S1.L1
